# Fritzing sketch shutters (saved by Fritzing 0.9.3b)
breadboards: 1

parts:
  Part1 = Arduino Mega 2560 (Rev3)
  S1 = SWITCH-MOMENTARY-2 [package=reed_switch_plastic]
  S2 = SWITCH-MOMENTARY-2 [package=reed_switch_plastic]
  S3 = SWITCH-MOMENTARY-2 [package=reed_switch_plastic]
  S4 = SWITCH-MOMENTARY-2 [package=reed_switch_plastic]
  S5 = SWITCH-MOMENTARY-2 [package=reed_switch_plastic]
  S6 = SWITCH-MOMENTARY-2 [package=reed_switch_plastic]
  S7 = SWITCH-MOMENTARY-2 [package=reed_switch_plastic]
  S8 = SWITCH-MOMENTARY-2 [package=reed_switch_plastic]
  Part2 = EasyDriver_v44
  Part3 = EasyDriver_v44
  Part4 = EasyDriver_v44
  Part5 = EasyDriver_v44
  M1 = Stepper Motor - Bipolar  # not connected
  M2 = Stepper Motor - Bipolar  # not connected
  M3 = Stepper Motor - Bipolar  # not connected
  M4 = Stepper Motor - Bipolar  # not connected
  R2 = Resistor [tolerance=±5% resistance=1k package=THT]
  R3 = Resistor [tolerance=±5% resistance=1k package=THT]
  R4 = Resistor [tolerance=±5% resistance=1k package=THT]
  R5 = Resistor [tolerance=±5% resistance=1k package=THT]  # not connected
  R6 = Resistor [tolerance=±5% resistance=1k package=THT]
  R7 = Resistor [tolerance=±5% resistance=1k package=THT]
  R8 = Resistor [tolerance=±5% resistance=1k package=THT]
  R9 = Resistor [tolerance=±5% resistance=1k package=THT]
  Part6 = Bluetooth HC-05 Macho
  R10 = PHOTOCELL [package=photocell]
  J1 = Piezo Speaker
  IR1 = TSOP312.., 314.. [package=THT]
  R11 = Resistor [tolerance=±5% resistance=1k package=THT]
  R12 = Resistor [tolerance=±5% resistance=100 package=THT]
  LED1 = smd LED [color="Red (633nm)" package="1206 [SMD]"]
  R13 = Resistor [tolerance=±5% resistance=1k package=THT]
  U1 = G3VM-61E1 [package=g3vm-61e1]

nets:
  N1: Part1.A0, R10.P$1, R11.Pin_1
  N2: Part1.D13_PWM, R13.Pin_0
  5V: Part1.5V, Part6.VCC, R10.P$2, IR1.Data, U1.P$4
  GND: Part1.GND, Part2.GND, Part3.GND, Part4.GND, Part5.GND, R2.Pin_1, R3.Pin_1, R4.Pin_1, R6.Pin_1, R7.Pin_1, R8.Pin_1, R9.Pin_1, Part6.GND, J1.pin1, IR1.Vs, R11.Pin_0, LED1.cathode, U1.P$5
  N3: Part1.VIN, U1.P$2
  N4: Part1.D0_RX0, Part6.TXD
  N5: Part1.D1_TX0, Part6.RXD
  N6: Part1.D2_PWM, R12.Pin_0
  N7: Part1.D3_PWM, IR1.GND
  N8: Part1.D4_PWM, U1.P$6
  N9: Part1.D22, Part2.STEP
  N10: Part1.D23, Part2.DIR
  N11: Part1.D24, Part3.STEP
  N12: Part1.D25, Part3.DIR
  N13: Part1.D26, Part4.STEP
  N14: Part1.D27, Part4.DIR
  N15: Part1.D28, Part5.STEP
  N16: Part1.D29, Part5.DIR
  N17: Part1.D32, S1.1, R6.Pin_0
  N18: Part1.D33, S2.1
  N19: Part1.D34, S3.1
  N20: Part1.D35, S4.1
  N21: Part1.D36, S5.1
  N22: Part1.D37, S6.1
  N23: Part1.D38, S7.1
  N24: Part1.D39, S8.1
  N25: Part2.V+, Part3.V+, Part4.V+, Part5.V+, U1.P$1
  N26: J1.pin2, R12.Pin_1
  N27: LED1.anode, R13.Pin_1

notes:
  1st shutter
  2nd shutter
  3d shutter
  4th shutter
  IN GND VCC
  NO COM NC
